# Fritzing sketch 1.3 (saved by Fritzing 1.0.3b)
breadboards: 1

parts:
  A1 = Arduino GIGA R1 WiFi
  L298N1 = L298N DC motor driver
  ZS-042_RTC1 = ZS-042 RTC Module
  L1 = Solenoid  # not connected
  VCC1 = Battery block 9V [internal_resistance=0.1Ω]
  J1 = Basic Servo
  Chirp!_Soil_Moisture_Sensor1 = Chirp! Soil Moisture Sensor v2.7.3

nets:
  N1: A1.Pin_32, Chirp!_Soil_Moisture_Sensor1.pin_3
  N2: A1.Pin_124, ZS-042_RTC1.SCL
  N3: A1.Pin_125, ZS-042_RTC1.SDA
  N4: A1.Pin_134, L298N1.IN1
  N5: A1.Pin_135, L298N1.IN2
  GND: L298N1.GND, ZS-042_RTC1.GND, VCC1.-, J1.gnd, Chirp!_Soil_Moisture_Sensor1.pin_5
  VCC: ZS-042_RTC1.VCC, J1.vcc, Chirp!_Soil_Moisture_Sensor1.Pin_1

custom parts:
  Arduino GIGA R1 WiFi: The Arduino GIGA R1 WiFi is designed for ambitious makers who want to step up their game.
  L298N DC motor driver: 2x DC motor driver with 78M05 positive voltage regulator (7..35 V) L298N: max 46 V, 2 A Set 5 V Enable jumper to enable 5 V regultor (needed for the L298N) and +5 V output at screw terminal or supply external +5 V at screw terminal Set ENA and/or ENB to +5 V to enable motor permanently or supply ENA and/or ENB with PWM signal IN1 and IN2 set rotation directory for motor A (OUT1/OUT2) IN2 and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
